# Fritzing sketch Projeto (saved by Fritzing 0.9.3b)

parts:
  Componente1 = Soil Moisture Sensor
  Componente3 = LCD1602-I2C
  U1 = ESP32S-HiLetgo [part_number=ESP32S-HiLetgo]
  DHT1 = DHT11 Humitidy and Temperature Sensor
  LED1 = LEDs [package=led10mm]
  Mod1 = KY-019 5V Relay Module [package="Breakout board"]
  VCC1 = 4 x AAA Battery Mount
  J1 = Basic Servo

nets:
  N1: Componente1.SIG, U1.GPIO25, DHT1.DATA
  GND: Componente1.GND, Componente3.GND, U1.GND, DHT1.GND, Mod1.-, J1.gnd
  VCC: Componente1.VCC, Componente3.VCC, U1.3.3, DHT1.VDD, J1.vcc
  N2: Componente3.SDA, U1.GPIO21
  N3: Componente3.SCL, U1.GPIO22
  N4: U1.VIN, Mod1.+
  N5: U1.GPIO16, Mod1.S
  N6: LED1.A, Mod1.Common
  N7: Mod1.NO, VCC1.+

custom parts:
  LCD1602-I2C: A standard character display, usually with 2x16 characters. Comes in many colors with LCM1602 IIC attached.
  ESP32S-HiLetgo: HiLetgo ESP-WROOM-32 ESP32 ESP-32S Development Board 2.4GHz Dual-Mode WiFi + Bluetooth Dual Cores Microcontroller The ESP32 integrated with Antenna switches, RF Balun, power amplifiers, low-noise amplifiers, filters, and management modules, and the entire solution occupies the least area of PCB. 2.4 GHz Wi-Fi plus Bluetooth dual-mode chip, with TSMC Ultra-low power consumption 40nm technology,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
  DHT11 Humitidy and Temperature Sensor: DHT11 Humidity and Temperature Sensor
  LEDs: LEDs Standard schematic elements and footprints for 5mm, 3mm, 1206, and 0603 sized LEDs. 5mm - Spark Fun Electronics SKU : COM-00529 (and others)
  KY-019 5V Relay Module: KY-019 5V Relay module, used to control AC circuits. (Special thanks to vanepp for fixing the PCB holes and other errors)

// code stored in the sketch: Projeto Micro.ino
#include "BluetoothSerial.h"
#include "ESP32Servo.h"
#if!defined(CONFIG_BT_ENABLED)||!defined(CONFIG_BLUEDROID_ENABLED)
#error Bluetooth is not enabled! Please run 'make menuconfig' to and enable it
#endif

BluetoothSerial SerialBT;
char valorRecebido;
void setup(){
  Serial.begin(115200);
  SerialBT.begin("cvu");
  Serial.println("Dispositivo");
  pinMode(relay,OUTPUT); // rel? 
}

void loop(){
//cedigo de ativacao da lampada rele
  valorRecebido = (char)SerialBT.read();
  if(Serial.available()){
    SerialBT.write(Serial.read());
  }
  if(SerialBT.available()){
    if(valorRecebido == 'Come?ar'){
      SerialBT.println("led aceso");
      digitalWrite(27,HIGH);
    }
    if(valorRecebido == 'Parar'){
      SerialBT.println("led apagado");
      digitalWrite(27,LOW);
    }
  }
  delay(50);
//fim do codigo ativacao lampada rele
}
